# Fritzing sketch blueboy (saved by Fritzing 0.9.6b)
breadboards: 1

parts:
  LLC1 = Logic Level Converter [package="Breakout board"]
  BT1 = Bluetooth HC-06u [package=THT]
  R2 = Resistor [tolerance=±5% resistance=10k package="0603 [SMD]"]
  R3 = Resistor [tolerance=±5% resistance=10k package="0603 [SMD]"]
  TP1 = TP4056 [chip_label=TP4056 package="DIP (Dual Inline) [THT]"]
  BAT1 = 18650 battery holder [package=battery-18650-kit]
  J1 = Dagu DGServo 9g header (male) [package=THT]
  Part1 = Arduino Uno (Rev3)
  S1 = Toggle Switch [package=THT]
  R4 = Resistor [tolerance=±5% resistance=2k package="0603 [SMD]"]
  Part3 = Adafruit BNO085 9-DOF Orientation IMU Fusion [part_number="Addfruit #4754"]

nets:
  N1: LLC1.LV1, J1.Vcc, Part3.SCL/SCK/RX
  N2: LLC1.LV2, J1.gnd, Part3.SDA/MISO/TX
  3V3: LLC1.LV, Part1.3V3, Part3.VCC
  GND: LLC1.L-GND, LLC1.H-GND, BT1.GND, TP1.pin6, J1.pulse, Part1.GND, Part3.GND
  N3: LLC1.LV4, BT1.RXD
  N4: LLC1.HV4, Part1.D9_PWM
  VCC: LLC1.HV, BT1.VCC, R2.Pin_0, R3.Pin_0, Part1.5V
  N5: LLC1.HV2, R2.Pin_1, Part1.A4/SDA
  N6: LLC1.HV1, R3.Pin_1, Part1.A5/SCL
  N7: BT1.TXD, Part1.D8
  N8: TP1.pin3, S1.COM
  N9: TP1.pin4, BAT1.+
  N10: TP1.pin5, BAT1.-
  N11: Part1.D3_PWM, Part3.INT
  N12: Part1.D4, R4.Pin_0
  N13: Part1.RESET, R4.Pin_1, Part3.RST
  N14: Part1.VIN, S1.L2

notes:
  External I2C
  Left: SDA
  Mid: SCL
  Right: GND

custom parts:
  Logic Level Converter: 5V to/from 3.3V logic level converter
  Bluetooth HC-06u: Bluetooth HC-06 - face up, pins down 16.5mm x 37.5mm PCB
  TP4056: A DIP stand-in part for whatever IC you want. With 6 pins on a 300mil dual inline package (DIP) footprint.
  18650 battery holder: 18650 Battery Holder
